# Fritzing sketch uTubo_MKI (saved by Fritzing 0.7.11b)
breadboards: 1

parts:
  F2 = Basic Flex Resistor
  F1 = Basic Flex Resistor
  Arduino1 = Arduino
  R6 = Resistor [tolerance=±5% resistance=10k package=THT]
  R5 = Resistor [tolerance=±5% resistance=10k package=THT]
  R8 = Resistor [tolerance=±5% resistance=10k package=THT]
  R7 = Resistor [tolerance=±5% resistance=10k package=THT]
  S1 = Round Pushbutton
  R9 = Resistor [tolerance=±5% resistance=10k package=THT]
  C2 = Ceramic Capacitor [capacitance=220nF package="100 mil [THT, multilayer]"]
  C1 = Ceramic Capacitor [capacitance=220nF package="100 mil [THT, multilayer]"]
  R2 = Resistor [tolerance=±1% resistance=680 package=THT]
  R1 = Resistor [tolerance=±1% resistance=680 package=THT]
  C3 = Ceramic Capacitor [capacitance=1nF package="100 mil [THT, multilayer]"]
  TRS2 = Stereo Jack (TRS) 3.5mm [package="PG203J [THT]"]
  R4 = Resistor [tolerance=±5% resistance=270 package=THT]
  C4 = Ceramic Capacitor [capacitance=100nF package="100 mil [THT, multilayer]"]
  M1 = SoftPot Membrane Potentiometer
  M2 = SoftPot Membrane Potentiometer
  R3 = Resistor [tolerance=±5% resistance=330 package=THT]

nets (from the breadboard view):
  N1: F2.Pin_2, F1.Pin_2, Arduino1.+5V, S1.leg0, S1.leg1, R9.Pin_0, M1.+V, M2.+V
  GND: F2.pin_1, F1.pin_1, Arduino1.GND, R6.Pin_0, R5.Pin_0, R8.Pin_0, R7.Pin_0, R2.Pin_1, C3.0, TRS2.Tip, M1.GND, M2.GND
  N2: Arduino1.D9, R4.Pin_0
  N3: Arduino1.D4, R9.Pin_1
  N4: Arduino1.A0, R6.Pin_1, M2.p
  N5: Arduino1.A1, R5.Pin_1, M1.p
  N6: Arduino1.A2, R8.Pin_1
  N7: Arduino1.A3, R7.Pin_1
  N8: C2.0, C3.1, R3.Pin_0
  N9: C2.1, R1.Pin_0, R4.Pin_1, C4.0
  N10: C1.0, TRS2.Sleeve, C4.1, R3.Pin_1
  N11: C1.1, R2.Pin_0, R1.Pin_1

notes:
  from arduino pin 9
  (for standard arduinos)
  3.5 mm jack audio out

custom parts:
  SoftPot Membrane Potentiometer: 200mm SoftPot Membrane Potentiometer
